# Fritzing sketch esp8266_blynk_temp_sensor (saved by Fritzing 0.9.3b)
breadboards: 1

parts:
  U1 = ESP8266 WiFi Module [part_number=ESP8266]
  DHT1 = DHT22 Humidity and Temperature Sensor
  R1 = Resistor [tolerance=±5% resistance=10k package="0402 [SMD]"]
  S1 = Momentary Switch [package=ksa_sealed_tac_switch]
  Part2 = USB converter CP2102
  IC1 = Voltage Regulator AMS1117 [package=sot223]
  DHT2 = DHT11 Humitidy and Temperature Sensor
  R2 = Resistor [tolerance=±5% resistance=10k package="0402 [SMD]"]

nets:
  N1: U1.RXD, Part2.TXO
  VDD: U1.VCC, U1.CH_PD, DHT1.VDD, R1.Pin_1, IC1.OUT, DHT2.VDD, R2.Pin_1
  N2: U1.GPIO_0, DHT1.DATA, R1.Pin_0, S1.2
  N3: U1.GPIO_2, DHT2.DATA, R2.Pin_0
  GND: U1.GND, DHT1.GND, S1.4, Part2.GND, IC1.GND, DHT2.GND
  N4: U1.TXD, Part2.RXI
  N5: Part2.+5V, IC1.IN

custom parts:
  ESP8266 WiFi Module: Generic WiFi Module based on the ESP8266 with onboard PCB antenna and UART communications
  DHT11 Humitidy and Temperature Sensor: DHT11 Humidity and Temperature Sensor
